# Fritzing sketch 02-led-steuern (saved by Fritzing 0.9.3b)
circuit board: 8.46667cm x 5.64444cm
breadboards: 1

parts:
  LED1 = smd LED [color="White (8000K)" package="0805 [SMD]"]
  R1 = Resistor [tolerance=±5% resistance=220 package=THT]
  A1 = Espressif ESP32-S3 Nano Development Board

nets:
  N1: LED1.cathode, A1.GND
  N2: LED1.anode, R1.Pin_1
  N3: R1.Pin_0, A1.02
