# Fritzing sketch 05-led-ueber-schalter-ansteuern (saved by Fritzing 0.9.3b)
breadboards: 1

parts:
  S1 = Pushbutton [package="[THT]"]
  LED2 = smd LED [color="Green (555nm)" package="0805 [SMD]"]
  R4 = Resistor [tolerance=±5% resistance=220 package=THT]
  A1 = Espressif ESP32-S3 Nano Development Board

nets:
  N1: S1.Pin_1, S1.Pin_2, LED2.cathode, A1.GND
  N2: S1.Pin_3, S1.Pin_4, A1.02
  N3: LED2.anode, R4.Pin_0
  N4: R4.Pin_1, A1.03
