# Fritzing sketch 07-servo-ansteuern (saved by Fritzing 0.9.3b)
breadboards: 1

parts:
  J1 = Basic Servo
  S2 = H-Bridge with L298N
  VCC2 = Battery block 9V
  A1 = Espressif ESP32-S3 Nano Development Board

nets:
  GND: J1.gnd, S2.GND, VCC2.-, A1.GND
  VCC: J1.vcc, S2.5V
  N1: J1.pulse, A1.05
  N2: S2.12V, VCC2.+

custom parts:
  H-Bridge with L298N: h-bridge
