# Fritzing sketch 08-lichtsensor-benutzen (saved by Fritzing 0.9.3b)
breadboards: 1

parts:
  R1 = PHOTOCELL [package=photocell]
  R2 = Resistor [tolerance=±5% resistance=1k package="0805 [SMD]"]
  A1 = Espressif ESP32-S3 Nano Development Board

nets:
  N1: R1.P$1, R2.Pin_1, A1.01
  N2: R2.Pin_0, A1.GND
